// Logisim project ICS233_PROJECT.circ as structural Verilog: 15 circuits, main circuit CPU
module Register_File (
  input  [15:0] BusW,
  input  [2:0] Rs1,
  input  [2:0] RD,
  input  [2:0] Rs2,
  input  RegWrite,
  input  Cllock,
  output [15:0] BusA,
  output [15:0] BusB
);

  wire and_1_out, and_2_out, and_3_out, and_4_out, and_5_out, and_6_out, and_7_out, decoder_1_out1,
       decoder_1_out2, decoder_1_out3, decoder_1_out4, decoder_1_out5, decoder_1_out6, decoder_1_out7;
  wire [15:0] register_1_q, register_2_q, register_3_q, register_4_q, register_5_q, register_6_q,
       register_7_q;

  Decoder #(.select(3), .enable("false")) decoder_1 (
    .out1(decoder_1_out1), .out2(decoder_1_out2), .out3(decoder_1_out3), .out4(decoder_1_out4),
    .out5(decoder_1_out5), .out6(decoder_1_out6), .out7(decoder_1_out7), .sel(RD));  // open: out0
  and and_1 (and_1_out, decoder_1_out1, RegWrite);
  and and_2 (and_2_out, decoder_1_out2, RegWrite);
  and and_3 (and_3_out, decoder_1_out3, RegWrite);
  and and_4 (and_4_out, decoder_1_out4, RegWrite);
  and and_5 (and_5_out, decoder_1_out5, RegWrite);
  and and_6 (and_6_out, decoder_1_out6, RegWrite);
  and and_7 (and_7_out, decoder_1_out7, RegWrite);
  Register #(.width(16)) register_1 (.D(BusW), .en(and_1_out), .Q(register_1_q), .clk(Cllock), .clr(1'b0));
  Register #(.width(16)) register_2 (.D(BusW), .en(and_2_out), .Q(register_2_q), .clk(Cllock), .clr(1'b0));
  Register #(.width(16)) register_3 (.D(BusW), .en(and_3_out), .Q(register_3_q), .clk(Cllock), .clr(1'b0));
  Register #(.width(16)) register_4 (.D(BusW), .en(and_4_out), .Q(register_4_q), .clk(Cllock), .clr(1'b0));
  Register #(.width(16)) register_5 (.D(BusW), .en(and_5_out), .Q(register_5_q), .clk(Cllock), .clr(1'b0));
  Register #(.width(16)) register_6 (.D(BusW), .en(and_6_out), .Q(register_6_q), .clk(Cllock), .clr(1'b0));
  Register #(.width(16)) register_7 (.D(BusW), .en(and_7_out), .Q(register_7_q), .clk(Cllock), .clr(1'b0));
  Multiplexer #(.select(3), .width(16), .enable("false")) multiplexer_1 (
    .in0({16{1'b0}}), .in1(register_1_q), .in2(register_2_q), .in3(register_3_q), .in4(register_4_q),
    .in5(register_5_q), .in6(register_6_q), .in7(register_7_q), .out(BusA), .sel(Rs1));
  Multiplexer #(.select(3), .width(16), .enable("false")) multiplexer_2 (
    .in0({16{1'b0}}), .in1(register_1_q), .in2(register_2_q), .in3(register_3_q), .in4(register_4_q),
    .in5(register_5_q), .in6(register_6_q), .in7(register_7_q), .out(BusB), .sel(Rs2));
endmodule

module Logic_Gate (
  input  [15:0] in_1,
  input  [15:0] in_2,
  input  [1:0] F,
  output [15:0] \output 
);

  wire [15:0] and_1_out, or_1_out, xor_1_out;

  assign and_1_out = in_1 & in_2;  // AND_Gate and_1, 16 bits wide
  assign or_1_out = in_1 | in_2;  // OR_Gate or_1, 16 bits wide
  assign xor_1_out = in_1 ^ in_2;  // XOR_Gate xor_1, 16 bits wide
  Multiplexer #(.select(2), .width(16), .enable("false")) multiplexer_1 (
    .in0(xor_1_out), .in1(or_1_out), .in2(and_1_out), .out(\output ), .sel(F));  // open: in3

  // Notes on the sheet:
  //   A
  //   B
endmodule

module Arithematic (
  input  [15:0] A,
  input  [15:0] B,
  input  [1:0] f,
  output [15:0] \output 
);

  wire comparator_1_lt, comparator_2_lt, xor_1_out;
  wire [15:0] adder_1_out, bit_extender_1_out, bit_extender_2_out, bit_extender_3_out, xor_2_out;

  xor xor_1 (xor_1_out, f[0], f[1]);
  assign bit_extender_1_out = {{15{xor_1_out}}, xor_1_out};  // Bit_Extender bit_extender_1
  assign xor_2_out = B ^ bit_extender_1_out;  // XOR_Gate xor_2, 16 bits wide
  Adder #(.width(16)) adder_1 (.a(A), .b(xor_2_out), .out(adder_1_out), .cin(xor_1_out));  // open: cout
  Comparator #(.width(16), .mode("unsigned")) comparator_1 (.a(A), .b(B), .lt(comparator_1_lt));  // open: gt, eq
  Comparator #(.width(16)) comparator_2 (.a(A), .b(B), .lt(comparator_2_lt));  // open: gt, eq
  assign bit_extender_2_out = {{15{1'b0}}, comparator_2_lt};  // Bit_Extender bit_extender_2
  assign bit_extender_3_out = {{15{1'b0}}, comparator_1_lt};  // Bit_Extender bit_extender_3
  Multiplexer #(.select(2), .width(16), .enable("false")) multiplexer_1 (
    .in0(adder_1_out), .in1(adder_1_out), .in2(bit_extender_2_out), .in3(bit_extender_3_out), .out(\output ),
    .sel(f));
endmodule

module Shifter (
  input  [15:0] in_1,
  input  [15:0] in_2,
  input  [1:0] F,
  output [15:0] Output
);

  wire [3:0] bit_extender_1_out;
  wire [15:0] shifter_1_out, shifter_2_out, shifter_3_out;

  Bit_Extender #(.in_width(16), .out_width(4)) bit_extender_1 (.in(in_2), .out(bit_extender_1_out));
  Shifter_part #(.width(16)) shifter_1 (.in(in_1), .\dist (bit_extender_1_out), .out(shifter_1_out));
  Shifter_part #(.width(16), .shift("lr")) shifter_2 (.in(in_1), .\dist (bit_extender_1_out), .out(shifter_2_out));
  Shifter_part #(.width(16), .shift("ar")) shifter_3 (.in(in_1), .\dist (bit_extender_1_out), .out(shifter_3_out));
  Multiplexer #(.select(2), .width(16), .enable("false")) multiplexer_1 (
    .in0(shifter_1_out), .in1(shifter_2_out), .in2(shifter_3_out), .out(Output), .sel(F));  // open: in3

  // Notes on the sheet:
  //   A
  //   B
endmodule

module CPU (
);

  wire Branch_Control, CLOCK, Imm5_Controller, MemRD_Controller, MemWR_Controller, RegW;
  wire [1:0] ALU_Controller, F, PC_Controller, RD_Controller, WB_Controller;
  wire [2:0] multiplexer_2_out, RD, Rs1, RS2;
  wire [4:0] imm2u_imm3l, imm5, OP;
  wire [10:0] imm11;
  wire [15:0] ALU_Output, bit_extender_1_out, bit_extender_2_out, bit_extender_3_out, bit_extender_4_out,
       BusA, BusA_imm5, BusB, BusW, Data_Memory_Output, multiplexer_1_out, multiplexer_3_out,
       multiplexer_4_out, PC, PC_1, PC__imm2U_imm3L, PC_imm11;

  Clock clock_1 (.out(CLOCK));
  PC_Normal_Adder pc_normal_adder_1 (.in_1(PC), .out_2(PC_1));
  Multiplexer #(.select(2), .width(16), .enable("false")) multiplexer_1 (
    .in0(PC_1), .in1(PC__imm2U_imm3L), .in2(PC_imm11), .in3(BusA_imm5), .out(multiplexer_1_out),
    .sel(PC_Controller));
  PC_Control pc_control_1 (.in_2(OP), .out_3(PC_Controller), .Branch_Control(Branch_Control));
  Branch_Control branch_control_1 (.BusA(BusA), .BusB(BusB), .OP(OP), .Output(Branch_Control));
  Jump_PC jump_pc_1 (.PC(PC), .imm11(imm11), .Output(PC_imm11));
  Register #(.width(16)) register_1 (.D(multiplexer_1_out), .en(1'b1), .Q(PC), .clk(CLOCK));  // open: clr
  Instruction_Memory instruction_memory_1 (
    .PC(PC), .imm2u_imm3l(imm2u_imm3l), .OP(OP), .Rd(RD), .Rs1(Rs1), .Rs2(RS2), .f(F), .imm11(imm11),
    .imm5(imm5));
  Branch_PC branch_pc_1 (.PC(PC), .Output(PC__imm2U_imm3L), .imm2u_imm3l(imm2u_imm3l));
  Control_Unit control_unit_1 (
    .in_1(OP), .out_2(WB_Controller), .out_3(MemWR_Controller), .out_4(MemRD_Controller),
    .out_5(ALU_Controller), .out_6(Imm5_Controller), .out_7(RegW), .out_8(RD_Controller));
  Multiplexer #(.select(2), .width(3), .enable("false")) multiplexer_2 (
    .in0(RD), .in1(3'b111), .in2(3'b001), .out(multiplexer_2_out), .sel(RD_Controller));  // open: in3
  JALR_PC jalr_pc_1 (.BusA(BusA), .imm5(imm5), .Output(BusA_imm5));
  Register_File register_file_1 (
    .BusW(BusW), .RD(multiplexer_2_out), .BusA(BusA), .Rs1(Rs1), .BusB(BusB), .Rs2(RS2), .RegWrite(RegW),
    .Cllock(CLOCK));
  assign bit_extender_1_out = {{11{1'b0}}, imm5};  // Bit_Extender bit_extender_1
  assign bit_extender_2_out = {{11{imm5[4]}}, imm5};  // Bit_Extender bit_extender_2
  Multiplexer #(.width(16), .enable("false")) multiplexer_3 (
    .in0(bit_extender_1_out), .in1(bit_extender_2_out), .out(multiplexer_3_out), .sel(Imm5_Controller));
  assign bit_extender_3_out = {{11{imm2u_imm3l[4]}}, imm2u_imm3l};  // Bit_Extender bit_extender_3
  assign bit_extender_4_out = {{5{imm11[10]}}, imm11};  // Bit_Extender bit_extender_4
  Multiplexer #(.select(2), .width(16), .enable("false")) multiplexer_4 (
    .in0(BusB), .in1(bit_extender_3_out), .in2(multiplexer_3_out), .in3(bit_extender_4_out),
    .out(multiplexer_4_out), .sel(ALU_Controller));
  ALU alu_1 (.in_1(BusA), .in_2(multiplexer_4_out), .F(F), .OP(OP), .Output(ALU_Output));
  Data_memory data_memory_1 (
    .address(ALU_Output), .data_in(BusB), .data_out(Data_Memory_Output), .MemRD(MemRD_Controller),
    .clock(CLOCK), .MemWR(MemWR_Controller));
  Multiplexer #(.select(2), .width(16), .enable("false")) multiplexer_5 (
    .in0(ALU_Output), .in1(Data_Memory_Output), .in2(PC_1), .out(BusW), .sel(WB_Controller));  // open: in3
endmodule

module ALU (
  input  [15:0] in_1,
  input  [15:0] in_2,
  input  [1:0] F,
  input  [4:0] OP,
  output [15:0] Output
);

  wire [1:0] multiplexer_1_out, multiplexer_3_out;
  wire [15:0] arithematic_1_output, logic_gate_1_output, shifter_1_output, shifter_3_out;

  Multiplexer #(.select(4), .width(2), .enable("false")) multiplexer_1 (
    .in0(F), .in1(F), .in2(F), .in3(2'b00), .in4(2'b10), .in5(2'b11), .in6(2'b00), .in7(2'b01), .in8(2'b10),
    .in9(2'b00), .in10(2'b01), .in11(2'b10), .in12(2'b00), .in13(2'b00), .out(multiplexer_1_out),
    .sel(OP[3:0]));  // open: in14, in15
  Logic_Gate logic_gate_1 (.in_1(in_1), .in_2(in_2), .F(multiplexer_1_out), .\output (logic_gate_1_output));
  Shifter shifter_1 (.in_1(in_1), .in_2(in_2), .F(multiplexer_1_out), .Output(shifter_1_output));
  Shifter shifter_2 (.in_1(in_1), .in_2(in_2), .F(multiplexer_1_out), .Output(shifter_1_output));
  Arithematic arithematic_1 (.A(in_1), .B(in_2), .\output (arithematic_1_output), .f(multiplexer_1_out));
  Shifter_part #(.width(16)) shifter_3 (.in(in_2), .\dist (4'b0101), .out(shifter_3_out));
  Multiplexer #(.select(2), .width(16), .enable("false")) multiplexer_2 (
    .in0(logic_gate_1_output), .in1(shifter_1_output), .in2(arithematic_1_output), .in3(shifter_3_out),
    .out(Output), .sel(multiplexer_3_out));
  Multiplexer #(.select(5), .width(2), .enable("false")) multiplexer_3 (
    .in0(2'b00), .in1(2'b01), .in2(2'b10), .in3(2'b10), .in4(2'b10), .in5(2'b10), .in6(2'b00), .in7(2'b00),
    .in8(2'b00), .in9(2'b01), .in10(2'b01), .in11(2'b01), .in12(2'b10), .in13(2'b10), .in20(2'b11),
    .in21(2'b11), .out(multiplexer_3_out), .sel(OP));  // open: in14, in15, in16, in17, in18, in19, in22, in23, in24, in25, in26, in27, in28, in29, in30, in31

  // Notes on the sheet:
  //   A
  //   B
endmodule

module Instruction_Memory (
  input  [15:0] PC,
  output [4:0] OP,
  output [2:0] Rd,
  output [2:0] Rs1,
  output [2:0] Rs2,
  output [1:0] f,
  output [10:0] imm11,
  output [4:0] imm2u_imm3l,
  output [4:0] imm5
);

  ROM #(.addrWidth(16), .dataWidth(16)) rom_1 (
    .addr(PC), .data({f, imm5[2:0], imm11[5:3], imm2u_imm3l[2:0], OP}));  // open: sel

  assign imm2u_imm3l[4:3] = f;
  assign imm5[4:3] = f;
  assign {imm11[10:6], imm11[2:0]} = {f, imm5[2:0], imm2u_imm3l[2:0]};
  assign Rd = imm2u_imm3l[2:0];
  assign Rs1 = imm11[5:3];
  assign Rs2 = imm5[2:0];

  // Notes on the sheet:
  //   contents of rom_1 (hex, n*v repeats v):
  //   1847 110d 1047 112d 3047 114d 4047 116d 847 118d 2847 fa43 50d1 968 87 a7 3cc bec 3791 3b0d 332d 887
  //   da3 b63 d50f a04f
endmodule

module Data_memory (
  input  [15:0] address,
  input  [15:0] data_in,
  input  MemWR,
  input  clock,
  input  MemRD,
  output [15:0] data_out
);

  RAM #(.addrWidth(16), .dataWidth(16), .bus("separate")) ram_1 (
    .addr(address), .din(data_in), .data(data_out), .str(MemWR), .clk(clock), .ld(MemRD));  // open: sel, clr
endmodule

module PC_Normal_Adder (
  input  [15:0] in_1,
  output [15:0] out_2
);

  Adder #(.width(16)) adder_1 (.a(16'h1), .b(in_1), .out(out_2));  // open: cin, cout
endmodule

module Jump_PC (
  input  [15:0] PC,
  input  [10:0] imm11,
  output [15:0] Output
);

  wire [15:0] bit_extender_1_out;

  assign bit_extender_1_out = {{5{imm11[10]}}, imm11};  // Bit_Extender bit_extender_1
  Adder #(.width(16)) adder_1 (.a(PC), .b(bit_extender_1_out), .out(Output));  // open: cin, cout
endmodule

module Branch_PC (
  input  [15:0] PC,
  input  [4:0] imm2u_imm3l,
  output [15:0] Output
);

  wire [15:0] bit_extender_1_out;

  assign bit_extender_1_out = {{11{imm2u_imm3l[4]}}, imm2u_imm3l};  // Bit_Extender bit_extender_1
  Adder #(.width(16)) adder_1 (.a(PC), .b(bit_extender_1_out), .out(Output));  // open: cin, cout
endmodule

module JALR_PC (
  input  [15:0] BusA,
  input  [4:0] imm5,
  output [15:0] Output
);

  wire [15:0] bit_extender_1_out;

  assign bit_extender_1_out = {{11{imm5[4]}}, imm5};  // Bit_Extender bit_extender_1
  Adder #(.width(16)) adder_1 (.a(BusA), .b(bit_extender_1_out), .out(Output));  // open: cin, cout
endmodule

module Control_Unit (
  input  [4:0] in_1,
  output [1:0] out_2,
  output out_3,
  output out_4,
  output [1:0] out_5,
  output out_6,
  output out_7,
  output [1:0] out_8
);

  wire [4:0] multiplexer_1_out;

  Multiplexer #(.select(5), .width(5), .enable("false")) multiplexer_1 (
    .in0({5{1'b0}}), .in1({5{1'b0}}), .in2({5{1'b0}}), .in3(5'b00001), .in4(5'b00001), .in5(5'b00001),
    .in6(5'b00010), .in7(5'b00010), .in8(5'b00010), .in9(5'b00011), .in10(5'b00011), .in11(5'b00011),
    .in12(5'b00100), .in13(5'b00101), .in14(5'b00110), .in15(5'b00110), .in16(5'b00110), .in17(5'b00110),
    .in18(5'b00110), .in19(5'b00110), .in20(5'b00111), .in21(5'b01000), .in22(5'b01001), .in23(5'b01010),
    .out(multiplexer_1_out), .sel(in_1));  // open: in24, in25, in26, in27, in28, in29, in30, in31
  ROM #(.addrWidth(5), .dataWidth(10)) rom_1 (
    .addr(multiplexer_1_out), .data({out_8, out_7, out_6, out_5, out_4, out_3, out_2}));  // open: sel

  // Notes on the sheet:
  //   contents of rom_1 (hex, n*v repeats v):
  //   80 e0 a0 a0 a9 14 10 2b0 0 2b2 b2
endmodule

module PC_Control (
  input  Branch_Control,
  input  [4:0] in_2,
  output [1:0] out_3
);

  wire [4:0] multiplexer_1_out, multiplexer_2_out;

  Multiplexer #(.width(5), .enable("false")) multiplexer_1 (
    .in0({5{1'b0}}), .in1(5'b00001), .out(multiplexer_1_out), .sel(Branch_Control));
  Multiplexer #(.select(5), .width(5), .enable("false")) multiplexer_2 (
    .in0({5{1'b0}}), .in1({5{1'b0}}), .in2({5{1'b0}}), .in3({5{1'b0}}), .in4({5{1'b0}}), .in5({5{1'b0}}),
    .in6({5{1'b0}}), .in7({5{1'b0}}), .in8({5{1'b0}}), .in9({5{1'b0}}), .in10({5{1'b0}}), .in11({5{1'b0}}),
    .in12({5{1'b0}}), .in13({5{1'b0}}), .in14(multiplexer_1_out), .in15(multiplexer_1_out),
    .in16(multiplexer_1_out), .in17(multiplexer_1_out), .in18(multiplexer_1_out), .in19(multiplexer_1_out),
    .in20({5{1'b0}}), .in21(5'b00010), .in22(5'b00010), .in23(5'b00011), .out(multiplexer_2_out), .sel(in_2));  // open: in24, in25, in26, in27, in28, in29, in30, in31
  ROM #(.addrWidth(5), .dataWidth(2)) rom_1 (.addr(multiplexer_2_out), .data(out_3));  // open: sel

  // Notes on the sheet:
  //   contents of rom_1 (hex, n*v repeats v):
  //   0 1 2 3
endmodule

module Branch_Control (
  input  [15:0] BusA,
  input  [15:0] BusB,
  input  [4:0] OP,
  output Output
);

  wire BEQ, BGE, BGEU, BLT, BLTU, BNE, comparator_1_eq, comparator_1_gt, comparator_2_gt;
  wire [4:0] subtractor_1_out;

  Comparator #(.width(16), .mode("unsigned")) comparator_1 (
    .a(BusA), .b(BusB), .gt(comparator_1_gt), .eq(comparator_1_eq), .lt(BLTU));
  Comparator #(.width(16)) comparator_2 (.a(BusA), .b(BusB), .gt(comparator_2_gt), .eq(BEQ), .lt(BLT));
  or or_1 (BGEU, comparator_1_gt, comparator_1_eq);
  or or_2 (BGE, comparator_2_gt, BEQ);
  not not_1 (BNE, BEQ);
  Subtractor #(.width(5)) subtractor_1 (.a(OP), .b(5'b01110), .out(subtractor_1_out));  // open: bin, bout
  Multiplexer #(.select(3), .enable("false")) multiplexer_1 (
    .in0(BEQ), .in1(BNE), .in2(BLT), .in3(BGE), .in4(BLTU), .in5(BGEU), .out(Output),
    .sel(subtractor_1_out[2:0]));  // open: in6, in7
endmodule
